# Fritzing sketch gate green radio (saved by Fritzing 0.9.3b)
breadboards: 1

parts:
  R2 = Resistor [tolerance=±5% resistance=220 package=THT]
  LED2 = LED - 5mm [color="Yellow (595nm)" package="5 mm [THT]"]
  Adafruit_Atmega32u1 = Adafruit Atmega32u4 Breakout Board [part_number="Atmega 32u4"]
  R3 = Resistor [tolerance=±5% resistance=10k package=THT]
  Part1 = LilyPad Button Board  # not connected
  R1 = Resistor [tolerance=±5% resistance=220 package=THT]
  LED1 = LED - 5mm [color="Red (660nm)" package="5 mm [THT]"]
  J1 = Piezo Speaker

nets:
  N1: R2.Pin_0, Adafruit_Atmega32u1.B2, R3.Pin_1, R1.Pin_0
  N2: R2.Pin_1, LED2.anode
  N3: LED2.cathode, Adafruit_Atmega32u1.B4
  N4: Adafruit_Atmega32u1.F7, Adafruit_Atmega32u1.B0, R3.Pin_0, J1.pin1
  N5: Adafruit_Atmega32u1.C6, J1.pin2
  N6: Adafruit_Atmega32u1.B5, LED1.anode
  N7: R1.Pin_1, LED1.cathode

notes:
  antenna
  Dipole Antenna
  GND
  3V
  D5
  D6
  D12
  Ground
  long legs (anodes)
  Gate Radio
  D10
  Connect TEST Jumper to 3v bus to invoke test mode for chekcing communication to mailbox and house. Disconnect for normal operation.
  TEST
