# Fritzing sketch mailbox red radio (saved by Fritzing 0.9.3b)
breadboards: 1

parts:
  R2 = Resistor [tolerance=±5% resistance=220 package=THT]
  LED2 = LED - 5mm [color="Green (560nm)" package="5 mm [THT]"]
  Adafruit_Atmega32u1 = Adafruit Atmega32u4 Breakout Board [part_number="Atmega 32u4"]
  R3 = Resistor [tolerance=±5% resistance=10k package=THT]
  S2 = Tilt Switch [package=THT]
  Part1 = LilyPad Button Board  # not connected
  R4 = Resistor [tolerance=±5% resistance=10k package=THT]
  SP1 = SPEAKER [package=pcb_mount_speaker]

nets:
  N1: R2.Pin_0, Adafruit_Atmega32u1.B6, Adafruit_Atmega32u1.B1, R3.Pin_1, R4.Pin_1, SP1.+, SP1.-
  N2: R2.Pin_1, LED2.anode
  N3: LED2.cathode, Adafruit_Atmega32u1.GND#14
  N4: Adafruit_Atmega32u1.C6, Adafruit_Atmega32u1.E6, S2.Pin_2, R4.Pin_0
  N5: Adafruit_Atmega32u1.B4, R3.Pin_0, S2.Pin_1

notes:
  antenna
  Dipole Antenna
  GND
  3V
  D5
  D6
  D12
  Ground
  long legs (anodes)
  Mailbox Radio
  Tilt Switch - attach to mailbox door
  D10
  TEST
  Connect TEST Jumper to 3v bus to invoke test mode for checking communication to gate. Disconnect for normal operation.
